// Logisim project HomeWork1.3.1.circ as structural Verilog: 1 circuit, main circuit main
module main (
  input  A,
  input  B,
  input  C,
  output out_4
);

  wire and_1_out, not_1_out, or_1_out;

  or or_1 (or_1_out, A, B, C);
  and and_1 (and_1_out, A, B, C);
  not not_1 (not_1_out, or_1_out);
  or or_2 (out_4, and_1_out, not_1_out);
endmodule
