// Logisim project HomeWork1.3.2.circ as structural Verilog: 1 circuit, main circuit main
module main (
  input  A,
  input  B,
  input  C,
  output out_4
);

  wire and_1_out, not_1_out, or_1_out;

  and and_1 (and_1_out, A, B, C);
  or or_1 (or_1_out, A, B, C);
  not not_1 (not_1_out, and_1_out);
  and and_2 (out_4, or_1_out, not_1_out);
endmodule
