// Logisim project Homework3.1.circ as structural Verilog: 1 circuit, main circuit main
module main (
  input  CLK,
  input  Din1,
  input  Din2,
  input  Din3,
  input  Din4,
  input  CLR,
  output out_7,
  output out_8,
  output out_9,
  output out_10
);

  D_Flip_Flop d_ff_1 (.clk(CLK), .D(Din1), .Q(out_7), .reset(CLR));  // open: Qn, preset, en
  D_Flip_Flop d_ff_2 (.clk(CLK), .D(Din2), .Q(out_8), .reset(CLR));  // open: Qn, preset, en
  D_Flip_Flop d_ff_3 (.clk(CLK), .D(Din3), .Q(out_9), .reset(CLR));  // open: Qn, preset, en
  D_Flip_Flop d_ff_4 (.clk(CLK), .D(Din4), .Q(out_10), .reset(CLR));  // open: Qn, preset, en
endmodule
